// Logisim project cola2_logisim.circ as structural Verilog: 1 circuit, main circuit main
module main (
  input  _5,
  input  _10,
  input  _50,
  input  Este_sau_nu_Cola,
  input  in_5,
  input  in_6,
  input  [7:0] in_7,
  input  [7:0] _100,
  output F3,
  output F4__Acceptare_moneda,
  output [7:0] out_11,
  output Drop_Cola,
  output [7:0] Suma,
  output [7:0] Moneda_introdusa,
  output [7:0] Rest
);

  wire and_8_out, and_9_out, and_10_out, and_12_out, and_13_out, and_14_out, and_15_out, and_16_out,
       clock_1_out, comparator_1_gt, comparator_2_eq, comparator_2_lt, or_1_out, or_2_out;
  wire [7:0] and_11_out, and_17_out, and_18_out;
  wire [7:7] button_1_out, comparator_2_gt;

  or or_1 (or_1_out, _5, _10, _50);
  or or_2 (or_2_out, _10, _50);
  not not_1 (F3, F4__Acceptare_moneda);
  and and_1 (F4__Acceptare_moneda, or_1_out, Este_sau_nu_Cola);
  and and_2 (Moneda_introdusa[5], F4__Acceptare_moneda, _50);
  and and_3 (Moneda_introdusa[4], F4__Acceptare_moneda, _50);
  and and_4 (Moneda_introdusa[3], F4__Acceptare_moneda, _10);
  and and_5 (Moneda_introdusa[2], F4__Acceptare_moneda, _5, _5);
  and and_6 (Moneda_introdusa[1], F4__Acceptare_moneda, or_2_out);
  and and_7 (Moneda_introdusa[0], F4__Acceptare_moneda, _5);
  and and_8 (and_8_out, comparator_2_lt, Suma[7]);
  Clock clock_1 (.out(clock_1_out));
  D_Flip_Flop d_ff_1 (
    .clk(clock_1_out), .D(and_8_out), .Q(out_11[7]), .reset(comparator_1_gt));  // open: Qn, preset, en
  and and_9 (and_9_out, comparator_2_lt, Suma[6]);
  D_Flip_Flop d_ff_2 (
    .clk(clock_1_out), .D(and_9_out), .Q(out_11[6]), .reset(comparator_1_gt));  // open: Qn, preset, en
  and and_10 (and_10_out, comparator_2_lt, Suma[5]);
  D_Flip_Flop d_ff_3 (
    .clk(clock_1_out), .D(and_10_out), .Q(out_11[5]), .reset(comparator_1_gt));  // open: Qn, preset, en
  assign and_11_out = out_11 & {8{button_1_out[7]}};  // AND_Gate and_11, 8 bits wide
  Comparator comparator_1 (.a(and_11_out), .b(in_7), .gt(comparator_1_gt));  // open: eq, lt
  and and_12 (and_12_out, comparator_2_lt, Suma[4]);
  D_Flip_Flop d_ff_4 (
    .clk(clock_1_out), .D(and_12_out), .Q(out_11[4]), .reset(comparator_1_gt));  // open: Qn, preset, en
  Button button_1 (.out(button_1_out[7]));
  and and_13 (and_13_out, comparator_2_lt, Suma[3]);
  D_Flip_Flop d_ff_5 (
    .clk(clock_1_out), .D(and_13_out), .Q(out_11[3]), .reset(comparator_1_gt));  // open: Qn, preset, en
  and and_14 (and_14_out, comparator_2_lt, Suma[2]);
  D_Flip_Flop d_ff_6 (
    .clk(clock_1_out), .D(and_14_out), .Q(out_11[2]), .reset(comparator_1_gt));  // open: Qn, preset, en
  Adder adder_1 (.a(out_11), .b({in_5, in_6, Moneda_introdusa[5:0]}), .out(Suma));  // open: cin, cout
  and and_15 (and_15_out, comparator_2_lt, Suma[1]);
  D_Flip_Flop d_ff_7 (
    .clk(clock_1_out), .D(and_15_out), .Q(out_11[1]), .reset(comparator_1_gt));  // open: Qn, preset, en
  Comparator comparator_2 (.a(Suma), .b(_100), .gt(comparator_2_gt[7]), .eq(comparator_2_eq), .lt(comparator_2_lt));
  and and_16 (and_16_out, comparator_2_lt, Suma[0]);
  or or_3 (Drop_Cola, comparator_2_gt[7], comparator_2_eq);
  D_Flip_Flop d_ff_8 (
    .clk(clock_1_out), .D(and_16_out), .Q(out_11[0]), .reset(comparator_1_gt));  // open: Qn, preset, en
  assign and_17_out = {8{comparator_2_gt[7]}} & Suma;  // AND_Gate and_17, 8 bits wide
  assign and_18_out = {8{comparator_2_gt[7]}} & _100;  // AND_Gate and_18, 8 bits wide
  Subtractor subtractor_1 (.a(and_17_out), .b(and_18_out), .out(Rest));  // open: bin, bout

  assign Moneda_introdusa[7:6] = {in_5, in_6};
endmodule
